# Fritzing sketch picam sketch (saved by Fritzing 0.9.3b)

parts:
  Raspberry_Pi1 = Raspberry Pi B+
  RTC = Real Time Clock Module - DS1307 RTC Breakout Board
  Script_bypass_switch = Pushbutton [package=THT]
  Current_limiting_resistor_for_switch = Resistor [tolerance=±5% resistance=12k package="2010 [SMD]"]
  Pulldown_resistor = Resistor [tolerance=±5% resistance=12k package="2010 [SMD]"]

nets:
  3V3: Raspberry_Pi1.3v3, Raspberry_Pi1.3V3, Current_limiting_resistor_for_switch.Pin_0
  N1: Raspberry_Pi1.GPIO2, RTC.SDA
  N2: Raspberry_Pi1.GPIO3, RTC.SCL
  GND: Raspberry_Pi1.GND, RTC.GND, Pulldown_resistor.Pin_1
  N3: Raspberry_Pi1.GPIO21, Script_bypass_switch.leg0, Pulldown_resistor.Pin_0
  5V: Raspberry_Pi1.5V, RTC.5V
  N4: Script_bypass_switch.leg1, Current_limiting_resistor_for_switch.Pin_1
